# Fritzing sketch arduino-metec-braille (saved by Fritzing 0.9.3b)

parts:
  Part1 = Metec DC-DC converter
  Part2 = Metec Braille line 20 cell
  Part3 = 8pin adapter
  Part4 = Arduino Uno (Rev3)

nets:
  N1: Part1.185V, Part3.200v
  N2: Part1.ON, Part4.D6_PWM
  N3: Part1.5V, Part3.5V#1
  N4: Part1.GND, Part3.GND#2
  N5: Part2.200V, Part3.200V
  N6: Part2.NC, Part3.NC
  N7: Part2.GND, Part3.GND#16
  N8: Part2.CLK, Part3.CLK#15
  N9: Part2.STRB, Part3.STRB#14
  N10: Part2.DIN, Part3.DIN#13
  N11: Part2.DOUT, Part3.DOUT#12
  N12: Part2.5V, Part3.5V#11
  N13: Part3.5V#3, Part4.5V
  N14: Part3.DOUT#4, Part4.D2
  N15: Part3.DIN#5, Part4.D3_PWM
  N16: Part3.STRB#6, Part4.D4
  N17: Part3.CLK#7, Part4.D5_PWM
  N18: Part3.GND#8, Part4.GND

custom parts:
  Metec DC-DC converter: DC-DC stepup switcher 5V to 185V
  Metec Braille line 20 cell: Braille-line with 20 x B11 Braille-cells with 8 Dots, driven by Piezo-actuators (bending type). Integrated drive electronic connected by an passive back-plane. Flat or concave tactile surface with one interaction button. Braille-line with 20 x B11 Braille-cells with 8 Dots, driven by Piezo-actuators (bending type). Integrated drive electronic connected by an passive back-plane. Flat or concave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
  8pin adapter: 8 pin adapter 2.00mm-2.54mm for Metec Braille line 20 cell standard
