# Fritzing sketch arduino-mini-metec-braille (saved by Fritzing 0.9.3b)

parts:
  Part6 = Metec DC-DC converter
  Part7 = Metec Braille line 20 cell
  Part8 = 8pin adapter
  Arduino1 = Arduino Mini (Rev5)

nets:
  N1: Part6.185V, Part8.200v
  N2: Part6.ON, Arduino1.D6_PWM
  N3: Part6.5V, Part8.5V#1
  N4: Part6.GND, Part8.GND#2
  N5: Part7.200V, Part8.200V
  N6: Part7.NC, Part8.NC
  N7: Part7.GND, Part8.GND#16
  N8: Part7.CLK, Part8.CLK#15
  N9: Part7.STRB, Part8.STRB#14
  N10: Part7.DIN, Part8.DIN#13
  N11: Part7.DOUT, Part8.DOUT#12
  N12: Part7.5V, Part8.5V#11
  N13: Part8.5V#3, Arduino1.5V
  N14: Part8.DOUT#4, Arduino1.D2
  N15: Part8.DIN#5, Arduino1.D3_PWM
  N16: Part8.STRB#6, Arduino1.D4
  N17: Part8.CLK#7, Arduino1.D5_PWM
  N18: Part8.GND#8, Arduino1.GND

custom parts:
  Metec DC-DC converter: DC-DC stepup switcher 5V to 185V
  Metec Braille line 20 cell: Braille-line with 20 x B11 Braille-cells with 8 Dots, driven by Piezo-actuators (bending type). Integrated drive electronic connected by an passive back-plane. Flat or concave tactile surface with one interaction button. Braille-line with 20 x B11 Braille-cells with 8 Dots, driven by Piezo-actuators (bending type). Integrated drive electronic connected by an passive back-plane. Flat or concave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
  8pin adapter: 8 pin adapter 2.00mm-2.54mm for Metec Braille line 20 cell standard
