# Fritzing sketch raspberry-metec-braille (saved by Fritzing 0.9.3b)

parts:
  Part9 = Metec DC-DC converter
  Part10 = Metec Braille line 20 cell
  Part11 = 8pin adapter
  Raspberry_Pi_A1 = Raspberry Pi A

nets:
  N1: Part9.185V, Part11.200v
  N2: Part9.ON, Raspberry_Pi_A1.GPIO_22
  N3: Part9.5V, Part11.5V#1
  N4: Part9.GND, Part11.GND#2
  N5: Part10.200V, Part11.200V
  N6: Part10.NC, Part11.NC
  N7: Part10.GND, Part11.GND#16
  N8: Part10.CLK, Part11.CLK#15
  N9: Part10.STRB, Part11.STRB#14
  N10: Part10.DIN, Part11.DIN#13
  N11: Part10.DOUT, Part11.DOUT#12
  N12: Part10.5V, Part11.5V#11
  N13: Part11.5V#3, Raspberry_Pi_A1.5V
  N14: Part11.DOUT#4, Raspberry_Pi_A1.GPIO_18
  N15: Part11.DIN#5, Raspberry_Pi_A1.GPIO_4
  N16: Part11.STRB#6, Raspberry_Pi_A1.GPIO_17
  N17: Part11.CLK#7, Raspberry_Pi_A1.GPIO_27
  N18: Part11.GND#8, Raspberry_Pi_A1.GND

custom parts:
  Metec DC-DC converter: DC-DC stepup switcher 5V to 185V
  Metec Braille line 20 cell: Braille-line with 20 x B11 Braille-cells with 8 Dots, driven by Piezo-actuators (bending type). Integrated drive electronic connected by an passive back-plane. Flat or concave tactile surface with one interaction button. Braille-line with 20 x B11 Braille-cells with 8 Dots, driven by Piezo-actuators (bending type). Integrated drive electronic connected by an passive back-plane. Flat or concave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
  8pin adapter: 8 pin adapter 2.00mm-2.54mm for Metec Braille line 20 cell standard
